// Logisim project project.circ as structural Verilog
module main (
  input  [31:0] in_1
);

  wire button_1_out, clock_1_out;
  wire [31:0] adder_1_out, register_1_q;

  Adder #(.width(32)) adder_1 (.a(32'h4), .out(adder_1_out));  // open: b, cin, cout
  Clock clock_1 (.out(clock_1_out));
  Button button_1 (.out(button_1_out));
  Register #(.width(32)) register_1 (
    .D(adder_1_out), .clk(clock_1_out), .Q(register_1_q), .clr(button_1_out));  // open: en
  ROM #(.dataWidth(32)) rom_1 (.addr(register_1_q[9:2]), .data(in_1));
endmodule
